# Fritzing sketch Three i2c devices on PCF8574 (saved by Fritzing 0.9.3b)
breadboards: 3

parts:
  Keypad4x1 = Keypad Membran 4x4
  esp1 = ESP32 DevKitc V4
  YwRobot_Power_Supply1 = YwRobot Breadboard Power Supply [part_number=545043]
  M1 = pcf8574 io expansion board [package=THT]
  M2 = pcf8574 io expansion board [package=THT]
  R1 = Resistor [tolerance=±5% resistance=10k package="0805 [SMD]"]
  R2 = Resistor [tolerance=±5% resistance=10k package="0805 [SMD]"]
  R3 = Resistor [tolerance=±5% resistance=10k package="0805 [SMD]"]
  R4 = Resistor [tolerance=±5% resistance=10k package="0805 [SMD]"]
  R5 = Resistor [tolerance=±5% resistance=10k package="0805 [SMD]"]
  R6 = Resistor [tolerance=±5% resistance=10k package="0805 [SMD]"]
  R7 = Resistor [tolerance=±5% resistance=10k package="0805 [SMD]"]
  R8 = Resistor [tolerance=±5% resistance=10k package="0805 [SMD]"]
  R9 = Resistor [tolerance=±5% resistance=10k package="0805 [SMD]"]
  LED1 = smd LED [color="Orange (620nm)" package="0805 [SMD]"]
  LED2 = smd LED [color="Yellow (592nm)" package="1206 [SMD]"]
  LED3 = smd LED [color="Red (633nm)" package="0603 [SMD]"]
  LED4 = smd LED [color="Green (565nm)" package="1206 [SMD]"]
  LED5 = smd LED [color="Blue (470nm)" package="1206 [SMD]"]
  LED6 = smd LED [color="White (6500K)" package="1206 [SMD]"]
  LED7 = smd LED [color="Orange (620nm)" package="1206 [SMD]"]
  LED8 = smd LED [color="Red (635nm)" package="1206 [SMD]"]
  Part1 = LCD1602-I2C

nets:
  N1: Keypad4x1.Pin1, M1.O7
  N2: Keypad4x1.Pin2, M1.O6
  N3: Keypad4x1.Pin3, M1.O5
  N4: Keypad4x1.Pin4, M1.O4
  N5: Keypad4x1.Pin5, M1.O3
  N6: Keypad4x1.Pin6, M1.O2
  N7: Keypad4x1.Pin7, M1.O1
  N8: Keypad4x1.Pin8, M1.O0
  N9: esp1.IO15, M1.INT, R9.Pin_0
  N10: esp1.IO21, M1.SDA, M2.SDA, Part1.SDA
  N11: esp1.IO22, M1.SCL, M2.SCL, Part1.SCL
  GND: esp1.GND#18, YwRobot_Power_Supply1.GND#13, YwRobot_Power_Supply1.GND#14, M1.GND, M2.GND, LED1.cathode, LED2.cathode, LED3.cathode, LED4.cathode, LED5.cathode, LED6.cathode, LED7.cathode, LED8.cathode, Part1.GND
  N12: esp1.3V3, YwRobot_Power_Supply1.VCC#5, YwRobot_Power_Supply1.VCC#6
  VCC: YwRobot_Power_Supply1.VCC#9, YwRobot_Power_Supply1.VCC#10, M1.VCC, M2.VCC, R9.Pin_1, Part1.VCC
  N13: YwRobot_Power_Supply1.GND#11, YwRobot_Power_Supply1.GND#12
  N14: M1.A2c, M1.A2-
  N15: M1.A1c, M1.A1-
  N16: M1.A0c, M1.A0-
  N17: M2.A2c, M2.A2-
  N18: M2.A1c, M2.A1-
  N19: M2.A0+, M2.A0c
  N20: M2.O0, R2.Pin_0
  N21: M2.O1, R1.Pin_0
  N22: M2.O2, R8.Pin_0
  N23: M2.O3, R7.Pin_0
  N24: M2.O4, R6.Pin_0
  N25: M2.O5, R5.Pin_0
  N26: M2.O6, R4.Pin_0
  N27: M2.O7, R3.Pin_0
  N28: R1.Pin_1, LED7.anode
  N29: R2.Pin_1, LED8.anode
  N30: R3.Pin_1, LED1.anode
  N31: R4.Pin_1, LED2.anode
  N32: R5.Pin_1, LED4.anode
  N33: R6.Pin_1, LED5.anode
  N34: R7.Pin_1, LED3.anode
  N35: R8.Pin_1, LED6.anode

custom parts:
  Keypad Membran 4x4: Membrane Keypad 4x4 Matrix
  ESP32 DevKitc V4: ESP32-DevKitC board with ESP32-WROOM-32 module. ESP32-DevKitC V4 is a small-sized ESP32-based development board produced by Espressif. Most of the pins on the ESP module are broken out to the pin headers on the board. The pins D0, D1, D2, D3, CMD and CLK are used internally for communication between ESP32 and SPI flash memory. They are grouped on both sides near the USB connector. Avoid using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
  YwRobot Breadboard Power Supply: The YwRobot Breadboard Power Supply (MB-V2) has two power rails; they can be 5V or 3V3. Power to the module can be provided through the female USB socket or through the A10 (female) 2.1mm power jack.
  pcf8574 io expansion board: pcf8574 io expansion board.
  LCD1602-I2C: A standard character display, usually with 2x16 characters. Comes in many colors with LCM1602 IIC attached.
